// Logisim project CPU.circ as structural Verilog: 12 circuits, main circuit CPU
module ALU (
  input  [15:0] A,
  input  [15:0] B,
  input  [3:0] sel,
  output [15:0] outputPin,
  output zr
);

  wire [0:0] comparator_2_eq;
  wire [15:0] adder_1_out, adder_2_out, adder_3_out, and_1_out, divider_1_out, multiplier_1_out,
       negator_1_out, not_1_out, or_1_out, shifter_1_out, shifter_2_out, shifter_3_out, shifter_4_out,
       subtractor_1_out, xor_1_out;

  assign and_1_out = A & B;  // AND_Gate and_1, 16 bits wide
  assign or_1_out = A | B;  // OR_Gate or_1, 16 bits wide
  assign not_1_out = ~A;  // NOT_Gate not_1, 16 bits wide
  assign xor_1_out = A ^ B;  // XOR_Gate xor_1, 16 bits wide
  Negator #(.width(16)) negator_1 (.in(A), .out(negator_1_out));
  Adder #(.width(16)) adder_1 (.a(A), .b(B), .out(adder_1_out));  // open: cin, cout
  Subtractor #(.width(16)) subtractor_1 (.a(A), .b(B), .out(subtractor_1_out));  // open: bin, bout
  Multiplier #(.width(16)) multiplier_1 (.a(A), .b(B), .out(multiplier_1_out));  // open: cin, cout
  Multiplexer #(.select(4), .width(16)) multiplexer_1 (
    .in0(and_1_out), .in1(or_1_out), .in2(xor_1_out), .in3(not_1_out), .in4(negator_1_out),
    .in5(adder_1_out), .in6(subtractor_1_out), .in7(multiplier_1_out), .in8(divider_1_out),
    .in9(adder_2_out), .in10(adder_3_out), .in11(shifter_1_out), .in12(shifter_2_out),
    .in13({{15{1'b0}}, comparator_2_eq[0]}), .in14(shifter_3_out), .in15(shifter_4_out), .out(outputPin),
    .sel(sel));
  Divider #(.width(16)) divider_1 (.a(A), .b(B), .out(divider_1_out));  // open: upper, rem
  Comparator #(.width(16)) comparator_1 (.a(outputPin), .b({16{1'b0}}), .eq(zr));  // open: gt, lt
  Adder #(.width(16)) adder_2 (.a(A), .b(16'h1), .out(adder_2_out));  // open: cin, cout
  Adder #(.width(16)) adder_3 (.a(A), .b(16'h1), .out(adder_3_out));  // open: cin, cout
  Shifter #(.width(16)) shifter_1 (.in(A), .\dist (B[3:0]), .out(shifter_1_out));
  Shifter #(.shift("lr"), .width(16)) shifter_2 (.in(A), .\dist (B[3:0]), .out(shifter_2_out));
  Comparator #(.width(16)) comparator_2 (.a(A), .b(B), .eq(comparator_2_eq[0]));  // open: gt, lt
  Shifter #(.shift("ar"), .width(16)) shifter_3 (.in(A), .\dist (B[3:0]), .out(shifter_3_out));
  Shifter #(.shift("rr"), .width(16)) shifter_4 (.in(A), .\dist (B[3:0]), .out(shifter_4_out));
endmodule

module DFlipFlop (
  input  D,
  input  clockPin,
  output Q,
  output NotQ
);

  wire nand_1_out, nand_2_out, not_1_out;

  not not_1 (not_1_out, D);
  nand nand_1 (nand_1_out, D, clockPin);
  nand nand_2 (nand_2_out, not_1_out, clockPin);
  nand nand_3 (Q, nand_1_out, NotQ);
  nand nand_4 (NotQ, Q, nand_2_out);
endmodule

module BitRegister (
  input  [15:0] inputPin,
  input  load,
  input  clockPin,
  input  reset,
  output [15:0] outputPin
);

  wire [15:0] multiplexer_1_out;

  Multiplexer #(.width(16)) multiplexer_1 (.in0(outputPin), .in1(inputPin), .out(multiplexer_1_out), .sel(load));
  Register #(.width(16)) register_1 (.D(multiplexer_1_out), .clk(clockPin), .Q(outputPin), .clr(reset));  // open: en
endmodule

module CPU (
  input  in_1,
  output halt
);

  wire alu_1_zr, demultiplexer_1_out0, demultiplexer_1_out1, demultiplexer_1_out2, demultiplexer_1_out3,
       demultiplexer_1_out4, demultiplexer_1_out5, demultiplexer_1_out6, demultiplexer_1_out7,
       MasterClock_out, multiplexer_7_out, opcodechecker_1_arithmetic, opcodechecker_1_clear,
       opcodechecker_1_db, opcodechecker_1_jmp, opcodechecker_1_jz, opcodechecker_1_ldr, opcodechecker_1_sb,
       opcodechecker_1_str, or_1_out, or_2_out, or_3_out, or_4_out;
  wire [2:0] InstructionMemory_p2_2, multiplexer_1_out, multiplexer_5_out;
  wire [3:0] InstructionMemory_p2_3;
  wire [14:0] programcounter_1_outputpin;
  wire [15:0] alu_1_outputpin, DataMemory_dout, InstructionMemory_p2, InstructionMemory_p3,
       multiplexer_2_out, multiplexer_3_out, multiplexer_4_out, multiplexer_6_out, multiplexer_8_out,
       multiplexer_9_out, multiplexer_10_out, multiplexer_11_out, R0_outputpin, R1_outputpin, R2_outputpin,
       R3_outputpin, R4_outputpin, R5_outputpin, R6_outputpin, R7_outputpin,
       registermuxsimplification_1_outputpin, registermuxsimplification_2_outputpin;

  ProgramCounter programcounter_1 (
    .inputPin(InstructionMemory_p3[14:0]), .reset(in_1), .load(or_4_out), .increment(1'b1),
    .inc2(opcodechecker_1_db), .clockPin(MasterClock_out), .outputPin(programcounter_1_outputpin));
  ALU alu_1 (
    .A(registermuxsimplification_2_outputpin), .B(registermuxsimplification_1_outputpin),
    .sel(InstructionMemory_p2_3), .outputPin(alu_1_outputpin), .zr(alu_1_zr));
  Demultiplexer #(.select(3)) demultiplexer_1 (
    .out0(demultiplexer_1_out0), .out1(demultiplexer_1_out1), .out2(demultiplexer_1_out2),
    .out3(demultiplexer_1_out3), .out4(demultiplexer_1_out4), .out5(demultiplexer_1_out5),
    .out6(demultiplexer_1_out6), .out7(demultiplexer_1_out7), .in(or_3_out), .sel(multiplexer_1_out));
  Multiplexer #(.width(3)) multiplexer_1 (
    .in0(InstructionMemory_p2_3[3:1]), .in1(InstructionMemory_p2_2), .out(multiplexer_1_out),
    .sel(opcodechecker_1_arithmetic));
  Clock MasterClock (.out(MasterClock_out));
  // ROM #(.addrWidth(15), .dataWidth(16), .line("dual"), .misaligned("true")) InstructionMemory: pin names not known; wires that end beside it: programcounter_1_outputpin, {InstructionMemory_p2[15:11], InstructionMemory_p2_3, InstructionMemory_p2_2, InstructionMemory_p2[3:0]}, InstructionMemory_p3
  Multiplexer #(.width(16)) multiplexer_2 (
    .in0(multiplexer_3_out), .in1({16{1'b0}}), .out(multiplexer_2_out), .sel(opcodechecker_1_clear));
  Multiplexer #(.width(16)) multiplexer_3 (
    .in0(multiplexer_4_out), .in1(alu_1_outputpin), .out(multiplexer_3_out), .sel(opcodechecker_1_arithmetic));
  Multiplexer #(.width(16)) multiplexer_4 (
    .in0(multiplexer_6_out), .in1(InstructionMemory_p3), .out(multiplexer_4_out), .sel(opcodechecker_1_db));
  Multiplexer #(.width(3)) multiplexer_5 (
    .in0({InstructionMemory_p2_3[0], InstructionMemory_p2_2[2:1]}), .in1(InstructionMemory_p2[3:1]),
    .out(multiplexer_5_out), .sel(opcodechecker_1_arithmetic));
  OpCodeChecker opcodechecker_1 (
    .OpCode(InstructionMemory_p2[15:11]), .ldr(opcodechecker_1_ldr), .str(opcodechecker_1_str),
    .db(opcodechecker_1_db), .sb(opcodechecker_1_sb), .arithmetic(opcodechecker_1_arithmetic),
    .jmp(opcodechecker_1_jmp), .jz(opcodechecker_1_jz), .clear(opcodechecker_1_clear), .endcode(halt));  // open: labelcode, scrnwrt
  Multiplexer #(.width(16)) multiplexer_6 (
    .in0({16{1'b0}}), .in1(DataMemory_dout), .out(multiplexer_6_out), .sel(opcodechecker_1_ldr));
  or or_1 (or_1_out, opcodechecker_1_ldr, opcodechecker_1_str, opcodechecker_1_sb);
  Multiplexer multiplexer_7 (.in0(1'b0), .in1(opcodechecker_1_jz), .out(multiplexer_7_out), .sel(alu_1_zr));
  BitRegister R0 (
    .inputPin(multiplexer_2_out), .load(demultiplexer_1_out0), .clockPin(MasterClock_out), .reset(in_1),
    .outputPin(R0_outputpin));
  BitRegister R1 (
    .inputPin(multiplexer_2_out), .load(demultiplexer_1_out1), .clockPin(MasterClock_out), .reset(in_1),
    .outputPin(R1_outputpin));
  BitRegister R2 (
    .inputPin(multiplexer_2_out), .load(demultiplexer_1_out2), .clockPin(MasterClock_out), .reset(in_1),
    .outputPin(R2_outputpin));
  BitRegister R3 (
    .inputPin(multiplexer_2_out), .load(demultiplexer_1_out3), .clockPin(MasterClock_out), .reset(in_1),
    .outputPin(R3_outputpin));
  BitRegister R4 (
    .inputPin(multiplexer_2_out), .load(demultiplexer_1_out4), .clockPin(MasterClock_out), .reset(in_1),
    .outputPin(R4_outputpin));
  BitRegister R5 (
    .inputPin(multiplexer_2_out), .load(demultiplexer_1_out5), .clockPin(MasterClock_out), .reset(in_1),
    .outputPin(R5_outputpin));
  BitRegister R6 (
    .inputPin(multiplexer_2_out), .load(demultiplexer_1_out6), .clockPin(MasterClock_out), .reset(in_1),
    .outputPin(R6_outputpin));
  BitRegister R7 (
    .inputPin(multiplexer_2_out), .load(demultiplexer_1_out7), .clockPin(MasterClock_out), .reset(in_1),
    .outputPin(R7_outputpin));
  Multiplexer #(.width(16)) multiplexer_8 (
    .in0(registermuxsimplification_1_outputpin), .in1(InstructionMemory_p3), .out(multiplexer_8_out),
    .sel(opcodechecker_1_sb));
  or or_2 (or_2_out, opcodechecker_1_str, opcodechecker_1_sb);
  or or_3 (or_3_out, opcodechecker_1_ldr, opcodechecker_1_str, opcodechecker_1_clear, opcodechecker_1_db, opcodechecker_1_arithmetic);
  or or_4 (or_4_out, opcodechecker_1_jmp, multiplexer_7_out);
  Multiplexer #(.width(16)) multiplexer_9 (
    .in0({16{1'b0}}), .in1(multiplexer_8_out), .out(multiplexer_9_out), .sel(or_1_out));
  RegisterMUXSimplification registermuxsimplification_1 (
    .R0toR3({R0_outputpin, R1_outputpin, R2_outputpin, R3_outputpin}),
    .R4toR7({R4_outputpin, R5_outputpin, R6_outputpin, R7_outputpin}), .sel(multiplexer_5_out),
    .outputPin(registermuxsimplification_1_outputpin));
  RegisterMUXSimplification registermuxsimplification_2 (
    .R0toR3({R0_outputpin, R1_outputpin, R2_outputpin, R3_outputpin}),
    .R4toR7({R4_outputpin, R5_outputpin, R6_outputpin, R7_outputpin}), .sel(multiplexer_1_out),
    .outputPin(registermuxsimplification_2_outputpin));
  Multiplexer #(.width(16)) multiplexer_10 (
    .in0(registermuxsimplification_2_outputpin), .in1(InstructionMemory_p3), .out(multiplexer_10_out),
    .sel(opcodechecker_1_sb));
  Multiplexer #(.width(16)) multiplexer_11 (
    .in0(multiplexer_9_out), .in1(registermuxsimplification_2_outputpin), .out(multiplexer_11_out),
    .sel(opcodechecker_1_sb));
  RAM #(.addrWidth(16), .clearpin("true"), .dataWidth(16)) DataMemory (
    .addr(multiplexer_11_out), .we(or_2_out), .oe(opcodechecker_1_ldr), .clk(MasterClock_out),
    .din(multiplexer_10_out), .dout(DataMemory_dout), .clr(in_1));

  // Notes on the sheet:
  //   contents of InstructionMemory (hex, n*v repeats v):
  //   4800 1700 65 1100 1 24f0 f20 2800 a 4800 1600 2 1e00 c 4000
endmodule

module PixelCounter (
  input  clockPin,
  input  reset,
  output [13:0] address,
  output [6:0] XOutput,
  output [6:0] YOutput
);

  wire XCounter_carry;
  wire [6:0] XCounter_q, YCounter_q;

  Counter #(.max('h7f), .width(14)) XCounter (
    .Q({XCounter_q, XOutput}), .carry(XCounter_carry), .clk(clockPin), .clr(reset));  // open: load, D, count, up
  Counter #(.max('h7f), .trigger("falling"), .width(14)) YCounter (
    .Q({YCounter_q, YOutput}), .clk(XCounter_carry), .clr(reset));  // open: load, D, count, carry, up
  Multiplier #(.width(14)) multiplier_1 (
    .a({YCounter_q, YOutput}), .b(14'h14), .out(address), .cin({XCounter_q, XOutput}));  // open: cout
endmodule

module Screen (
  input  in_1,
  input  [15:0] in_2,
  input  clockPin,
  input  reset,
  input  writeEnable
);

  wire [6:0] pixelcounter_1_xoutput, pixelcounter_1_youtput;
  wire [13:0] pixelcounter_1_address;
  wire [15:0] ScreenMemory_dout;

  PixelCounter pixelcounter_1 (
    .clockPin(clockPin), .reset(reset), .address(pixelcounter_1_address), .XOutput(pixelcounter_1_xoutput),
    .YOutput(pixelcounter_1_youtput));
  RAM #(.addrWidth(14), .dataWidth(16)) ScreenMemory (
    .addr(pixelcounter_1_address), .we(in_1), .oe(in_1), .clk(clockPin), .din(in_2), .dout(ScreenMemory_dout));
  // RGB_Video #(.cursor("No Cursor"), .scale(8)) rgb_video_1: pin names not known; wires that end beside it: clockPin, writeEnable, pixelcounter_1_xoutput, pixelcounter_1_youtput, ScreenMemory_dout
endmodule

module ProgramCounter (
  input  [14:0] inputPin,
  input  reset,
  input  load,
  input  increment,
  input  inc2,
  input  clockPin,
  output [14:0] outputPin
);

  wire or_1_out, or_2_out;
  wire [14:0] adder_1_out, multiplexer_1_out, multiplexer_2_out, multiplexer_3_out, multiplexer_4_out,
       multiplexer_5_out;

  Multiplexer #(.width(15)) multiplexer_1 (.in0(15'h1), .in1(15'h2), .out(multiplexer_1_out), .sel(inc2));
  Adder #(.width(15)) adder_1 (.a(outputPin), .b(multiplexer_1_out), .out(adder_1_out));  // open: cin, cout
  Multiplexer #(.width(15)) multiplexer_2 (
    .in0(outputPin), .in1(adder_1_out), .out(multiplexer_2_out), .sel(increment));
  Multiplexer #(.width(15)) multiplexer_3 (
    .in0(multiplexer_2_out), .in1(inputPin), .out(multiplexer_3_out), .sel(load));
  Multiplexer #(.width(15)) multiplexer_4 (
    .in0(multiplexer_3_out), .in1({15{1'b0}}), .out(multiplexer_4_out), .sel(reset));
  or or_1 (or_1_out, load, increment);
  or or_2 (or_2_out, or_1_out, reset);
  Multiplexer #(.width(15)) multiplexer_5 (
    .in0(outputPin), .in1(multiplexer_4_out), .out(multiplexer_5_out), .sel(or_2_out));
  Register #(.width(15)) register_1 (.D(multiplexer_5_out), .clk(clockPin), .Q(outputPin));  // open: en, clr
endmodule

module InstructionDecoder (
  input  [10:0] flags,
  input  [4:0] OpCode,
  output [2:0] out_3,
  output [15:0] AddressBus
);

  OpCodeChecker opcodechecker_1 (.OpCode(OpCode));  // open: ldr, str, db, sb, arithmetic, jmp, jz, clear, endcode, labelcode, scrnwrt
  Multiplexer #(.width(16)) multiplexer_1 (.in1({16{1'b0}}), .out(AddressBus));  // open: in0, sel

  assign out_3 = flags[10:8];
endmodule

module OpCodeChecker (
  input  [4:0] OpCode,
  output ldr,
  output str,
  output db,
  output sb,
  output arithmetic,
  output jmp,
  output jz,
  output clear,
  output endcode,
  output labelcode,
  output scrnwrt
);

  wire not_1_out, not_2_out, not_3_out, not_4_out, not_5_out;

  not not_1 (not_1_out, OpCode[4]);
  not not_2 (not_2_out, OpCode[3]);
  not not_3 (not_3_out, OpCode[2]);
  not not_4 (not_4_out, OpCode[1]);
  not not_5 (not_5_out, OpCode[0]);
  and and_1 (ldr, not_1_out, not_2_out, not_3_out, not_4_out, not_5_out);
  and and_2 (str, not_1_out, not_2_out, not_3_out, not_4_out, OpCode[0]);
  and and_3 (db, not_1_out, not_2_out, not_3_out, OpCode[1], not_5_out);
  and and_4 (sb, not_1_out, not_2_out, not_3_out, OpCode[1], OpCode[0]);
  and and_5 (arithmetic, not_1_out, not_2_out, OpCode[2], not_4_out, not_5_out);
  and and_6 (jmp, not_1_out, not_2_out, OpCode[2], not_4_out, OpCode[0]);
  and and_7 (jz, not_1_out, not_2_out, OpCode[2], OpCode[1], not_5_out);
  and and_8 (clear, not_1_out, not_2_out, OpCode[2], OpCode[1], OpCode[0]);
  and and_9 (endcode, not_1_out, OpCode[3], not_3_out, not_4_out, not_5_out);
  and and_10 (labelcode, not_1_out, OpCode[3], not_3_out, not_4_out, OpCode[0]);
  and and_11 (scrnwrt, not_1_out, OpCode[3], not_3_out, OpCode[1], not_5_out);
endmodule

module RegisterMUXSimplification (
  input  [63:0] R0toR3,
  input  [63:0] R4toR7,
  input  [2:0] sel,
  output [15:0] outputPin
);

  Multiplexer #(.select(3), .width(16)) multiplexer_1 (
    .in0(R0toR3[63:48]), .in1(R0toR3[47:32]), .in2(R0toR3[31:16]), .in3(R0toR3[15:0]), .in4(R4toR7[63:48]),
    .in5(R4toR7[47:32]), .in6(R4toR7[31:16]), .in7(R4toR7[15:0]), .out(outputPin), .sel(sel));
endmodule

module OldALU (
  input  zx,
  input  nx,
  input  zy,
  input  ny,
  input  f,
  input  no,
  input  [15:0] in_7,
  input  [15:0] in_8,
  output zr,
  output ng,
  output [15:0] out_11
);

  wire or_1_out;
  wire [15:0] adder_1_out, and_1_out, multiplexer_1_out, multiplexer_2_out, multiplexer_3_out,
       multiplexer_4_out, multiplexer_5_out, not_1_out, not_2_out, not_3_out;

  Multiplexer #(.width(16)) multiplexer_1 (.in0(in_7), .in1({16{1'b0}}), .out(multiplexer_1_out), .sel(zx));
  Multiplexer #(.width(16)) multiplexer_2 (.in0(in_8), .in1({16{1'b0}}), .out(multiplexer_2_out), .sel(zy));
  assign not_1_out = ~multiplexer_1_out;  // NOT_Gate not_1, 16 bits wide
  assign not_2_out = ~multiplexer_2_out;  // NOT_Gate not_2, 16 bits wide
  Multiplexer #(.width(16)) multiplexer_3 (.in0(multiplexer_1_out), .in1(not_1_out), .out(multiplexer_3_out), .sel(nx));
  Multiplexer #(.width(16)) multiplexer_4 (.in0(multiplexer_2_out), .in1(not_2_out), .out(multiplexer_4_out), .sel(ny));
  assign and_1_out = multiplexer_3_out & multiplexer_4_out;  // AND_Gate and_1, 16 bits wide
  Adder #(.width(16)) adder_1 (.a(multiplexer_3_out), .b(multiplexer_4_out), .out(adder_1_out));  // open: cin, cout
  Multiplexer #(.width(16)) multiplexer_5 (.in0(and_1_out), .in1(adder_1_out), .out(multiplexer_5_out), .sel(f));
  assign not_3_out = ~multiplexer_5_out;  // NOT_Gate not_3, 16 bits wide
  Multiplexer #(.width(16)) multiplexer_6 (
    .in0(multiplexer_5_out), .in1(not_3_out), .out({ng, out_11[14:0]}), .sel(no));
  or or_1 (or_1_out, out_11[0], out_11[1], out_11[2], out_11[3], out_11[4], out_11[5], out_11[6], out_11[7], out_11[8], out_11[9], out_11[10], out_11[11], out_11[12], out_11[13], out_11[14], ng);
  not not_4 (zr, or_1_out);

  assign out_11[15] = ng;
endmodule

module TestScreen (
  input  in_1,
  input  in_2,
  output [15:0] out_3,
  output halt
);

  wire alu_1_zr, demultiplexer_1_out0, demultiplexer_1_out1, demultiplexer_1_out2, demultiplexer_1_out3,
       demultiplexer_1_out4, demultiplexer_1_out5, demultiplexer_1_out6, demultiplexer_1_out7,
       InstructionMemory_p1, multiplexer_7_out, opcodechecker_1_arithmetic, opcodechecker_1_clear,
       opcodechecker_1_db, opcodechecker_1_jmp, opcodechecker_1_jz, opcodechecker_1_ldr, opcodechecker_1_sb,
       opcodechecker_1_scrnwrt, opcodechecker_1_str, or_1_out, or_2_out, or_3_out, or_4_out, or_5_out,
       screen_clock;
  wire [2:0] InstructionMemory_p3_2, multiplexer_1_out, multiplexer_5_out;
  wire [3:0] InstructionMemory_p3_3;
  wire [6:0] X_coord, Y_coord;
  wire [13:0] multiplexer_10_out, multiplier_1_out, pixelcounter_1_address;
  wire [14:0] programcounter_1_outputpin;
  wire [15:0] alu_1_outputpin, DataMemory_dout, InstructionMemory_p3, InstructionMemory_p4,
       multiplexer_2_out, multiplexer_3_out, multiplexer_4_out, multiplexer_6_out, multiplexer_8_out,
       multiplexer_9_out, multiplexer_11_out, multiplexer_12_out, R0_outputpin, R1_outputpin, R2_outputpin,
       R3_outputpin, R4_outputpin, R5_outputpin, R7_outputpin, RGB_data, X_value, Y_value;

  ProgramCounter programcounter_1 (
    .inputPin(InstructionMemory_p4[14:0]), .reset(in_1), .load(or_4_out), .increment(1'b1), .inc2(or_5_out),
    .clockPin(InstructionMemory_p1), .outputPin(programcounter_1_outputpin));
  ALU alu_1 (.A(Y_value), .B(X_value), .sel(InstructionMemory_p3_3), .outputPin(alu_1_outputpin), .zr(alu_1_zr));
  Demultiplexer #(.select(3)) demultiplexer_1 (
    .out0(demultiplexer_1_out0), .out1(demultiplexer_1_out1), .out2(demultiplexer_1_out2),
    .out3(demultiplexer_1_out3), .out4(demultiplexer_1_out4), .out5(demultiplexer_1_out5),
    .out6(demultiplexer_1_out6), .out7(demultiplexer_1_out7), .in(or_3_out), .sel(multiplexer_1_out));
  Multiplexer #(.width(3)) multiplexer_1 (
    .in0(InstructionMemory_p3_3[3:1]), .in1(InstructionMemory_p3_2), .out(multiplexer_1_out),
    .sel(opcodechecker_1_arithmetic));
  // ROM #(.addrWidth(15), .dataWidth(16), .line("dual"), .misaligned("true")) InstructionMemory: pin names not known; wires that end beside it: InstructionMemory_p1, programcounter_1_outputpin, {InstructionMemory_p3[15:11], InstructionMemory_p3_3, InstructionMemory_p3_2, InstructionMemory_p3[3:0]}, InstructionMemory_p4
  Multiplexer #(.width(16)) multiplexer_2 (
    .in0(multiplexer_3_out), .in1({16{1'b0}}), .out(multiplexer_2_out), .sel(opcodechecker_1_clear));
  Multiplexer #(.width(16)) multiplexer_3 (
    .in0(multiplexer_4_out), .in1(alu_1_outputpin), .out(multiplexer_3_out), .sel(opcodechecker_1_arithmetic));
  Multiplexer #(.width(16)) multiplexer_4 (
    .in0(multiplexer_6_out), .in1(InstructionMemory_p4), .out(multiplexer_4_out), .sel(opcodechecker_1_db));
  // RGB_Video rgb_video_1: pin names not known; wires that end beside it: in_2, screen_clock, 1'b1, X_coord, Y_coord, RGB_data
  Multiplexer #(.width(3)) multiplexer_5 (
    .in0({InstructionMemory_p3_3[0], InstructionMemory_p3_2[2:1]}), .in1(InstructionMemory_p3[3:1]),
    .out(multiplexer_5_out), .sel(opcodechecker_1_arithmetic));
  OpCodeChecker opcodechecker_1 (
    .OpCode(InstructionMemory_p3[15:11]), .ldr(opcodechecker_1_ldr), .str(opcodechecker_1_str),
    .db(opcodechecker_1_db), .sb(opcodechecker_1_sb), .arithmetic(opcodechecker_1_arithmetic),
    .jmp(opcodechecker_1_jmp), .jz(opcodechecker_1_jz), .clear(opcodechecker_1_clear), .endcode(halt),
    .scrnwrt(opcodechecker_1_scrnwrt));  // open: labelcode
  Multiplexer #(.width(16)) multiplexer_6 (
    .in0({16{1'b0}}), .in1(DataMemory_dout), .out(multiplexer_6_out), .sel(opcodechecker_1_ldr));
  or or_1 (or_1_out, opcodechecker_1_ldr, opcodechecker_1_str, opcodechecker_1_sb);
  Multiplexer multiplexer_7 (.in0(1'b0), .in1(opcodechecker_1_jz), .out(multiplexer_7_out), .sel(alu_1_zr));
  BitRegister R0 (
    .inputPin(multiplexer_2_out), .load(demultiplexer_1_out0), .clockPin(InstructionMemory_p1), .reset(in_1),
    .outputPin(R0_outputpin));
  BitRegister R1 (
    .inputPin(multiplexer_2_out), .load(demultiplexer_1_out1), .clockPin(InstructionMemory_p1), .reset(in_1),
    .outputPin(R1_outputpin));
  BitRegister R2 (
    .inputPin(multiplexer_2_out), .load(demultiplexer_1_out2), .clockPin(InstructionMemory_p1), .reset(in_1),
    .outputPin(R2_outputpin));
  BitRegister R3 (
    .inputPin(multiplexer_2_out), .load(demultiplexer_1_out3), .clockPin(InstructionMemory_p1), .reset(in_1),
    .outputPin(R3_outputpin));
  BitRegister R4 (
    .inputPin(multiplexer_2_out), .load(demultiplexer_1_out4), .clockPin(InstructionMemory_p1), .reset(in_1),
    .outputPin(R4_outputpin));
  BitRegister R5 (
    .inputPin(multiplexer_2_out), .load(demultiplexer_1_out5), .clockPin(InstructionMemory_p1), .reset(in_1),
    .outputPin(R5_outputpin));
  BitRegister R6 (
    .inputPin(multiplexer_2_out), .load(demultiplexer_1_out6), .clockPin(InstructionMemory_p1), .reset(in_1),
    .outputPin(out_3));
  BitRegister R7 (
    .inputPin(multiplexer_2_out), .load(demultiplexer_1_out7), .clockPin(InstructionMemory_p1), .reset(in_1),
    .outputPin(R7_outputpin));
  Multiplexer #(.width(16)) multiplexer_8 (
    .in0(X_value), .in1(InstructionMemory_p4), .out(multiplexer_8_out), .sel(opcodechecker_1_sb));
  or or_2 (or_2_out, opcodechecker_1_str, opcodechecker_1_sb);
  or or_3 (or_3_out, opcodechecker_1_ldr, opcodechecker_1_str, opcodechecker_1_clear, opcodechecker_1_db, opcodechecker_1_arithmetic);
  or or_4 (or_4_out, opcodechecker_1_jmp, multiplexer_7_out);
  or or_5 (or_5_out, opcodechecker_1_db, opcodechecker_1_scrnwrt);
  Multiplexer #(.width(16)) multiplexer_9 (
    .in0({16{1'b0}}), .in1(multiplexer_8_out), .out(multiplexer_9_out), .sel(or_1_out));
  Clock clock_1 (.out(screen_clock));
  RegisterMUXSimplification registermuxsimplification_1 (
    .R0toR3({R0_outputpin, R1_outputpin, R2_outputpin, R3_outputpin}),
    .R4toR7({R4_outputpin, R5_outputpin, out_3, R7_outputpin}), .sel(multiplexer_5_out), .outputPin(X_value));
  RegisterMUXSimplification registermuxsimplification_2 (
    .R0toR3({R0_outputpin, R1_outputpin, R2_outputpin, R3_outputpin}),
    .R4toR7({R4_outputpin, R5_outputpin, out_3, R7_outputpin}), .sel(multiplexer_1_out), .outputPin(Y_value));
  PixelCounter pixelcounter_1 (
    .clockPin(screen_clock), .reset(opcodechecker_1_scrnwrt), .address(pixelcounter_1_address),
    .XOutput(X_coord), .YOutput(Y_coord));
  Multiplier #(.width(14)) multiplier_1 (
    .a(Y_value[13:0]), .b(14'h80), .out(multiplier_1_out), .cin(X_value[13:0]));  // open: cout
  Multiplexer #(.width(14)) multiplexer_10 (
    .in0(pixelcounter_1_address), .in1(multiplier_1_out), .out(multiplexer_10_out),
    .sel(opcodechecker_1_scrnwrt));
  Multiplexer #(.width(16)) multiplexer_11 (
    .in0(Y_value), .in1(InstructionMemory_p4), .out(multiplexer_11_out), .sel(opcodechecker_1_sb));
  Multiplexer #(.width(16)) multiplexer_12 (
    .in0(multiplexer_9_out), .in1(Y_value), .out(multiplexer_12_out), .sel(opcodechecker_1_sb));
  RAM #(.addrWidth(14), .clearpin("true"), .dataWidth(16)) ScreenMemory (
    .addr(multiplexer_10_out), .we(opcodechecker_1_scrnwrt), .oe(1'b1), .clk(InstructionMemory_p1),
    .din(InstructionMemory_p4), .dout(RGB_data), .clr(in_1));
  RAM #(.addrWidth(16), .clearpin("true"), .dataWidth(16)) DataMemory (
    .addr(multiplexer_12_out), .we(or_2_out), .oe(opcodechecker_1_ldr), .clk(InstructionMemory_p1),
    .din(multiplexer_11_out), .dout(DataMemory_dout), .clr(in_1));

  // Notes on the sheet:
  //   contents of InstructionMemory (hex, n*v repeats v):
  //   4800 1000 a 1100 a 4800 5020 e2 1400 1d 11a0 3000 f 2480 2800 5 4800 1000 a 1100 b 4800 5020 e2 1000
  //   1d 5020 e2 1400 26 11a1 3000 23 2490 1000 a 2800 14 4800 1000 a 1100 27 4800 5020 e2 1400 1d 11a0
  //   3000 2480 2800 28 4000
endmodule
